// Logisim project MAQUINA MOORE ASC DESC.circ as structural Verilog: 1 circuit, main circuit main
module main (
  input  X,
  output S2,
  output S3,
  output J1,
  output K1,
  output J2,
  output K2,
  output J3,
  output K3
);

  wire and_1_out, and_2_out, and_3_out, and_4_out, and_5_out, and_6_out, and_7_out, and_8_out, clock_1_out,
       j_k_ff_1_q, not_1_out, not_2_out, not_3_out, not_4_out, not_5_out, not_6_out, not_7_out, not_8_out,
       not_9_out, not_10_out, not_11_out, not_12_out;

  not not_1 (not_1_out, S2);
  and and_1 (and_1_out, not_1_out, not_2_out, not_3_out);
  not not_2 (not_2_out, S3);
  not not_3 (not_3_out, X);
  and and_2 (and_2_out, S2, S3, X);
  not not_4 (not_4_out, S3);
  and and_3 (and_3_out, not_4_out, not_5_out);
  not not_5 (not_5_out, X);
  and and_4 (and_4_out, S3, X);
  not not_6 (not_6_out, j_k_ff_1_q);
  and and_5 (and_5_out, not_6_out, S3, X);
  and and_6 (and_6_out, j_k_ff_1_q, not_7_out, not_8_out);
  not not_7 (not_7_out, S3);
  not not_8 (not_8_out, X);
  not not_9 (not_9_out, S3);
  and and_7 (and_7_out, not_9_out, not_10_out);
  not not_10 (not_10_out, X);
  and and_8 (and_8_out, S3, X);
  not not_11 (not_11_out, j_k_ff_1_q);
  or or_1 (J3, not_11_out, not_12_out);
  not not_12 (not_12_out, S2);
  or or_2 (J1, and_1_out, and_2_out);
  or or_3 (K1, and_3_out, and_4_out, S2);
  or or_4 (J2, and_5_out, and_6_out);
  or or_5 (K2, and_7_out, and_8_out, j_k_ff_1_q);
  Clock clock_1 (.out(clock_1_out));
  J_K_Flip_Flop j_k_ff_1 (.J(J1), .clk(clock_1_out), .K(K1), .Q(j_k_ff_1_q));  // open: Qn, preset, en, reset
  J_K_Flip_Flop j_k_ff_2 (.J(J2), .clk(clock_1_out), .K(K2), .Q(S2));  // open: Qn, preset, en, reset
  LED led_1 (.in(j_k_ff_1_q));
  J_K_Flip_Flop j_k_ff_3 (.J(J3), .clk(clock_1_out), .K(1'b1), .Q(S3));  // open: Qn, preset, en, reset

  assign K3 = 1'b1;

  // Notes on the sheet:
  //   1
  //   2
  //   3
endmodule
